# Fritzing sketch MP3,Alarm (saved by Fritzing 0.9.3b)
breadboards: 1

parts:
  Part1 = Arduino Mega 2560 (Rev3)
  ZS-042_RTC1 = ZS-042 RTC Module
  DFRobot_DFPlayer_Mini1 = DFRobot DFPlayer Mini [part_number=DFR0299]
  SP1 = SPEAKER [package=pcb_mount_speaker]
  R1 = Resistor [tolerance=±5% resistance=470 package="2010 [SMD]"]

nets:
  N1: Part1.D19/RX1, DFRobot_DFPlayer_Mini1.TX
  N2: Part1.D18/TX1, R1.Pin_0
  N3: Part1.SCL, ZS-042_RTC1.SCL
  N4: Part1.SDA, ZS-042_RTC1.SDA
  GND: Part1.GND, ZS-042_RTC1.GND, DFRobot_DFPlayer_Mini1.GND-1, DFRobot_DFPlayer_Mini1.GND-2
  VCC: Part1.5V, ZS-042_RTC1.VCC, DFRobot_DFPlayer_Mini1.VCC
  N5: DFRobot_DFPlayer_Mini1.RX, R1.Pin_1
  N6: DFRobot_DFPlayer_Mini1.SPK_1, SP1.-
  N7: DFRobot_DFPlayer_Mini1.SPK_2, SP1.+
  N8: DFRobot_DFPlayer_Mini1.IO_2, DFRobot_DFPlayer_Mini1.ADKEY_1, DFRobot_DFPlayer_Mini1.ADKEY_2, DFRobot_DFPlayer_Mini1.USB_POS, DFRobot_DFPlayer_Mini1.USB_NEG
